// Logisim project 150119510_150118019_150119804_150118882.circ as structural Verilog: 17 circuits, main circuit main
module main (
);

  wire adder_1_overflow, alu_1_branch_output, clock_1_out, control_unit_1_enable_write,
       control_unit_1_pc_increment, control_unit_1_use_immediate, Enable_Inp, is_Branch, Load_Data, or_1_out,
       or_2_out, Store_Data;
  wire [2:0] Addr3, NZP;
  wire [3:0] multiplexer_4_out, multiplexer_5_out, OPcode, Reg1, Reg2, Reg3;
  wire [5:0] ImmTunnel;
  wire [9:0] Addr10, multiplexer_1_out, register_1_q;
  wire [13:0] Pc_Imm;
  wire [17:0] adder_1_result, Addr3Ext, alu_1_result, Data, multiplexer_2_out, multiplexer_3_out,
       n6_18_extender_1_output, n14_18_extender_1_output, program_counter_1_next_address,
       registers_1_register_1_data, registers_1_register_2_data, rom_1_data;

  _6_18_Extender u_6_18_extender_1 (.Input(ImmTunnel), .Output(n6_18_extender_1_output));
  Clock clock_1 (.out(clock_1_out));
  or or_1 (or_1_out, Store_Data, Load_Data);
  Program_Counter program_counter_1 (
    .Enable_Input(Enable_Inp), .JumpTo(adder_1_result), .Next_Address(program_counter_1_next_address),
    .Clear(1'b0), .Clock(clock_1_out), .Enable_Clock(control_unit_1_pc_increment));
  Multiplexer #(.width(10), .enable("false")) multiplexer_1 (
    .in0(register_1_q), .in1(Addr10), .out(multiplexer_1_out), .sel(or_1_out));
  _14_18_Extender u_14_18_extender_1 (.Input(Pc_Imm), .Output(n14_18_extender_1_output));
  Control_Unit control_unit_1 (
    .Clock(clock_1_out), .Pc_Increment(control_unit_1_pc_increment), .Pc_Enable_Input(Enable_Inp),
    .Enable_Write(control_unit_1_enable_write), .Data_Enable_Store(Store_Data),
    .Use_Immediate(control_unit_1_use_immediate), .Branch_Output(alu_1_branch_output),
    .Data_Enable_Load(Load_Data), .OPcode(OPcode));
  ALU alu_1 (
    .Src2(registers_1_register_2_data), .Imm(n6_18_extender_1_output), .Src1(registers_1_register_1_data),
    .NZP(NZP), .Use_Immediate(control_unit_1_use_immediate), .Opcode(OPcode), .Result(alu_1_result),
    .Branch_Output(alu_1_branch_output));
  Multiplexer #(.width(18), .enable("false")) multiplexer_2 (
    .in0(n14_18_extender_1_output), .in1(Addr3Ext), .out(multiplexer_2_out), .sel(is_Branch));
  RAM #(.addrWidth(10), .dataWidth(18), .bus("separate")) ram_1 (
    .addr(multiplexer_1_out), .din(registers_1_register_1_data), .data(Data), .str(Store_Data),
    .clk(clock_1_out), .ld(1'b1));  // open: sel, clr
  Register #(.width(10)) register_1 (.D(multiplexer_1_out), .Q(register_1_q), .clk(clock_1_out));  // open: en, clr
  Adder adder_1 (
    .Src1(multiplexer_2_out), .Src2(program_counter_1_next_address), .Overflow(adder_1_overflow),
    .Result(adder_1_result));
  ROM #(.addrWidth(18), .dataWidth(18)) rom_1 (.addr(program_counter_1_next_address), .data(rom_1_data));  // open: sel
  Multiplexer #(.width(18), .enable("false")) multiplexer_3 (
    .in0(alu_1_result), .in1(Data), .out(multiplexer_3_out), .sel(Load_Data));
  Registers registers_1 (
    .Data_Input(multiplexer_3_out), .Read_From_1(multiplexer_5_out), .Read_From_2(multiplexer_4_out),
    .Register_1_Data(registers_1_register_1_data), .Register_2_Data(registers_1_register_2_data),
    .Write_To(Reg1), .Enable_Write(control_unit_1_enable_write), .Clock(clock_1_out));
  Splitter splitter_1 (
    .Input(rom_1_data), .OpCode(OPcode), .Reg1(Reg1), .Address10(Addr10), .Reg3(Reg3), .Imm_Addr6(ImmTunnel),
    .NZP(NZP), .Reg2(Reg2), .Addr3(Addr3), .Addr14(Pc_Imm));
  or or_2 (or_2_out, Store_Data, is_Branch);
  Multiplexer #(.width(4), .enable("false")) multiplexer_4 (
    .in0(Reg3), .in1(Reg2), .out(multiplexer_4_out), .sel(is_Branch));
  Multiplexer #(.width(4), .enable("false")) multiplexer_5 (
    .in0(Reg2), .in1(Reg1), .out(multiplexer_5_out), .sel(or_2_out));
  Is_Branch is_branch_1 (.Opcode(OPcode), .Is_Branch(is_Branch));
  _3_18_Extender u_3_18_extender_1 (.Input(Addr3), .Output(Addr3Ext));
  // also tied to GND on the sheet: adder_1_overflow

  // Notes on the sheet:
  //   contents of rom_1 (hex, n*v repeats v):
  //   12a9b 13b81 13f40 13780 3b7c 2e693 12641 23ffb 2bc00
endmodule

module Full_Adder (
  input  Cin,
  input  Src1,
  input  Src2,
  output Sum,
  output Cout
);

  wire and_1_out, and_2_out, xor_1_out;

  xor xor_1 (xor_1_out, Src1, Src2);
  xor xor_2 (Sum, Cin, xor_1_out);
  and and_1 (and_1_out, Src1, Src2);
  and and_2 (and_2_out, xor_1_out, Cin);
  or or_1 (Cout, and_1_out, and_2_out);
endmodule

module Adder (
  input  [17:0] Src1,
  input  [17:0] Src2,
  output [17:0] Result,
  output Overflow
);

  wire _0_cout, _1_cout, _2_cout, _3_cout, _4_cout, _5_cout, _6_cout, _7_cout, _8_cout, _9_cout, _10_cout,
       _11_cout, _12_cout, _13_cout, _14_cout, _15_cout, _16_cout;

  Full_Adder _0 (.Cin(1'b0), .Src1(Src1[0]), .Src2(Src2[0]), .Sum(Result[0]), .Cout(_0_cout));
  Full_Adder _1 (.Cin(_0_cout), .Src1(Src1[1]), .Src2(Src2[1]), .Sum(Result[1]), .Cout(_1_cout));
  Full_Adder _2 (.Cin(_1_cout), .Src1(Src1[2]), .Src2(Src2[2]), .Sum(Result[2]), .Cout(_2_cout));
  Full_Adder _3 (.Cin(_2_cout), .Src1(Src1[3]), .Src2(Src2[3]), .Sum(Result[3]), .Cout(_3_cout));
  Full_Adder _4 (.Cin(_3_cout), .Src1(Src1[4]), .Src2(Src2[4]), .Sum(Result[4]), .Cout(_4_cout));
  Full_Adder _5 (.Cin(_4_cout), .Src1(Src1[5]), .Src2(Src2[5]), .Sum(Result[5]), .Cout(_5_cout));
  Full_Adder _6 (.Cin(_5_cout), .Src1(Src1[6]), .Src2(Src2[6]), .Sum(Result[6]), .Cout(_6_cout));
  Full_Adder _7 (.Cin(_6_cout), .Src1(Src1[7]), .Src2(Src2[7]), .Sum(Result[7]), .Cout(_7_cout));
  Full_Adder _8 (.Cin(_7_cout), .Src1(Src1[8]), .Src2(Src2[8]), .Sum(Result[8]), .Cout(_8_cout));
  Full_Adder _9 (.Cin(_8_cout), .Src1(Src1[9]), .Src2(Src2[9]), .Sum(Result[9]), .Cout(_9_cout));
  Full_Adder _10 (.Cin(_9_cout), .Src1(Src1[10]), .Src2(Src2[10]), .Sum(Result[10]), .Cout(_10_cout));
  Full_Adder _11 (.Cin(_10_cout), .Src1(Src1[11]), .Src2(Src2[11]), .Sum(Result[11]), .Cout(_11_cout));
  Full_Adder _12 (.Cin(_11_cout), .Src1(Src1[12]), .Src2(Src2[12]), .Sum(Result[12]), .Cout(_12_cout));
  Full_Adder _13 (.Cin(_12_cout), .Src1(Src1[13]), .Src2(Src2[13]), .Sum(Result[13]), .Cout(_13_cout));
  Full_Adder _14 (.Cin(_13_cout), .Src1(Src1[14]), .Src2(Src2[14]), .Sum(Result[14]), .Cout(_14_cout));
  Full_Adder _15 (.Cin(_14_cout), .Src1(Src1[15]), .Src2(Src2[15]), .Sum(Result[15]), .Cout(_15_cout));
  Full_Adder _16 (.Cin(_15_cout), .Src1(Src1[16]), .Src2(Src2[16]), .Sum(Result[16]), .Cout(_16_cout));
  Full_Adder _17 (.Cin(_16_cout), .Src1(Src1[17]), .Src2(Src2[17]), .Sum(Result[17]), .Cout(Overflow));
endmodule

module ALU (
  input  Use_Immediate,
  input  [17:0] Src2,
  input  [17:0] Imm,
  input  [3:0] Opcode,
  input  [17:0] Src1,
  input  [2:0] NZP,
  output [17:0] Result,
  output Branch_Output
);

  wire adder_1_overflow;
  wire [17:0] adder_1_result, and_1_out, multiplexer_1_out, or_1_out, xor_1_out;

  Multiplexer #(.width(18), .enable("false")) multiplexer_1 (
    .in0(Src2), .in1(Imm), .out(multiplexer_1_out), .sel(Use_Immediate));
  Adder adder_1 (.Src1(multiplexer_1_out), .Src2(Src1), .Overflow(adder_1_overflow), .Result(adder_1_result));
  assign and_1_out = multiplexer_1_out & Src1;  // AND_Gate and_1, 18 bits wide
  assign or_1_out = multiplexer_1_out | Src1;  // OR_Gate or_1, 18 bits wide
  assign xor_1_out = multiplexer_1_out ^ Src1;  // XOR_Gate xor_1, 18 bits wide
  Branch_Circuit branch_circuit_1 (.nzp(NZP), .OP1(Src1), .OP2(Src2), .Output(Branch_Output));
  Multiplexer #(.select(4), .width(18), .enable("false")) multiplexer_2 (
    .in0(adder_1_result), .in1(and_1_out), .in2(or_1_out), .in3(xor_1_out), .in4(adder_1_result),
    .in5(and_1_out), .in6(or_1_out), .in7(xor_1_out), .in8({18{1'b0}}), .in9({18{1'b0}}), .in10({18{1'b0}}),
    .in11({18{1'b0}}), .in12({18{1'b0}}), .in13({18{1'b0}}), .in14({18{1'b0}}), .in15({18{1'b0}}),
    .out(Result), .sel(Opcode));
  // also tied to GND on the sheet: adder_1_overflow
endmodule

module Registers (
  input  [3:0] Write_To,
  input  Enable_Write,
  input  Clock,
  input  [17:0] Data_Input,
  input  [3:0] Read_From_1,
  input  [3:0] Read_From_2,
  output [17:0] Register_1_Data,
  output [17:0] Register_2_Data
);

  wire and_1_out, and_2_out, and_3_out, and_4_out, and_5_out, and_6_out, and_7_out, and_8_out, and_9_out,
       and_10_out, and_11_out, and_12_out, and_13_out, and_14_out, and_15_out, and_16_out, decoder_1_out0,
       decoder_1_out1, decoder_1_out2, decoder_1_out3, decoder_1_out4, decoder_1_out5, decoder_1_out6,
       decoder_1_out7, decoder_1_out8, decoder_1_out9, decoder_1_out10, decoder_1_out11, decoder_1_out12,
       decoder_1_out13, decoder_1_out14, decoder_1_out15;
  wire [17:0] R0_q, R1_q, R2_q, R3_q, R4_q, R5_q, R6_q, R7_q, R8_q, R9_q, R10_q, R11_q, R12_q, R13_q, R14_q,
       R15_q;

  Decoder #(.select(4), .enable("false")) decoder_1 (
    .out0(decoder_1_out0), .out1(decoder_1_out1), .out2(decoder_1_out2), .out3(decoder_1_out3),
    .out4(decoder_1_out4), .out5(decoder_1_out5), .out6(decoder_1_out6), .out7(decoder_1_out7),
    .out8(decoder_1_out8), .out9(decoder_1_out9), .out10(decoder_1_out10), .out11(decoder_1_out11),
    .out12(decoder_1_out12), .out13(decoder_1_out13), .out14(decoder_1_out14), .out15(decoder_1_out15),
    .sel(Write_To));
  and and_1 (and_1_out, decoder_1_out0, Enable_Write);
  and and_2 (and_2_out, decoder_1_out1, Enable_Write);
  and and_3 (and_3_out, decoder_1_out2, Enable_Write);
  and and_4 (and_4_out, decoder_1_out3, Enable_Write);
  and and_5 (and_5_out, decoder_1_out4, Enable_Write);
  and and_6 (and_6_out, decoder_1_out5, Enable_Write);
  and and_7 (and_7_out, decoder_1_out6, Enable_Write);
  and and_8 (and_8_out, decoder_1_out7, Enable_Write);
  Register #(.width(18)) R0 (.D(Data_Input), .en(and_1_out), .Q(R0_q), .clk(Clock));  // open: clr
  Register #(.width(18)) R1 (.D(Data_Input), .en(and_2_out), .Q(R1_q), .clk(Clock));  // open: clr
  Register #(.width(18)) R2 (.D(Data_Input), .en(and_3_out), .Q(R2_q), .clk(Clock));  // open: clr
  Register #(.width(18)) R3 (.D(Data_Input), .en(and_4_out), .Q(R3_q), .clk(Clock));  // open: clr
  Register #(.width(18)) R4 (.D(Data_Input), .en(and_5_out), .Q(R4_q), .clk(Clock));  // open: clr
  Register #(.width(18)) R5 (.D(Data_Input), .en(and_6_out), .Q(R5_q), .clk(Clock));  // open: clr
  Register #(.width(18)) R6 (.D(Data_Input), .en(and_7_out), .Q(R6_q), .clk(Clock));  // open: clr
  Register #(.width(18)) R7 (.D(Data_Input), .en(and_8_out), .Q(R7_q), .clk(Clock));  // open: clr
  and and_9 (and_9_out, decoder_1_out8, Enable_Write);
  and and_10 (and_10_out, decoder_1_out9, Enable_Write);
  and and_11 (and_11_out, decoder_1_out10, Enable_Write);
  and and_12 (and_12_out, decoder_1_out11, Enable_Write);
  and and_13 (and_13_out, decoder_1_out12, Enable_Write);
  and and_14 (and_14_out, decoder_1_out13, Enable_Write);
  and and_15 (and_15_out, decoder_1_out14, Enable_Write);
  and and_16 (and_16_out, decoder_1_out15, Enable_Write);
  Register #(.width(18)) R8 (.D(Data_Input), .en(and_9_out), .Q(R8_q), .clk(Clock));  // open: clr
  Register #(.width(18)) R9 (.D(Data_Input), .en(and_10_out), .Q(R9_q), .clk(Clock));  // open: clr
  Register #(.width(18)) R10 (.D(Data_Input), .en(and_11_out), .Q(R10_q), .clk(Clock));  // open: clr
  Register #(.width(18)) R11 (.D(Data_Input), .en(and_12_out), .Q(R11_q), .clk(Clock));  // open: clr
  Register #(.width(18)) R12 (.D(Data_Input), .en(and_13_out), .Q(R12_q), .clk(Clock));  // open: clr
  Register #(.width(18)) R13 (.D(Data_Input), .en(and_14_out), .Q(R13_q), .clk(Clock));  // open: clr
  Register #(.width(18)) R14 (.D(Data_Input), .en(and_15_out), .Q(R14_q), .clk(Clock));  // open: clr
  Register #(.width(18)) R15 (.D(Data_Input), .en(and_16_out), .Q(R15_q), .clk(Clock));  // open: clr
  Multiplexer #(.select(4), .width(18), .enable("false")) multiplexer_1 (
    .in0(R0_q), .in1(R1_q), .in2(R2_q), .in3(R3_q), .in4(R4_q), .in5(R5_q), .in6(R6_q), .in7(R7_q),
    .in8(R8_q), .in9(R9_q), .in10(R10_q), .in11(R11_q), .in12(R12_q), .in13(R13_q), .in14(R14_q),
    .in15(R15_q), .out(Register_1_Data), .sel(Read_From_1));
  Multiplexer #(.select(4), .width(18), .enable("false")) multiplexer_2 (
    .in0(R0_q), .in1(R1_q), .in2(R2_q), .in3(R3_q), .in4(R4_q), .in5(R5_q), .in6(R6_q), .in7(R7_q),
    .in8(R8_q), .in9(R9_q), .in10(R10_q), .in11(R11_q), .in12(R12_q), .in13(R13_q), .in14(R14_q),
    .in15(R15_q), .out(Register_2_Data), .sel(Read_From_2));
endmodule

module Splitter (
  input  [17:0] Input,
  output [3:0] OpCode,
  output [3:0] Reg1,
  output [9:0] Address10,
  output [3:0] Reg3,
  output [5:0] Imm_Addr6,
  output [3:0] Reg2,
  output [2:0] Addr3,
  output [13:0] Addr14,
  output [2:0] NZP
);


  assign Addr3 = Input[2:0];
  assign Addr14 = Input[13:0];
  assign Address10 = Input[9:0];
  assign Imm_Addr6 = Input[5:0];
  assign NZP = Input[5:3];
  assign OpCode = Input[17:14];
  assign Reg1 = Input[13:10];
  assign Reg2 = Input[9:6];
  assign Reg3 = Input[5:2];
endmodule

// PC
module Program_Counter (
  input  Enable_Input,
  input  [17:0] JumpTo,
  input  Enable_Clock,
  input  Clock,
  input  Clear,
  output [17:0] Next_Address
);

  wire adder_1_overflow;
  wire [17:0] adder_1_result, multiplexer_1_out;

  Multiplexer #(.width(18), .enable("false")) multiplexer_1 (
    .in0(adder_1_result), .in1(JumpTo), .out(multiplexer_1_out), .sel(Enable_Input));
  Register #(.width(18)) register_1 (
    .D(multiplexer_1_out), .en(Enable_Clock), .Q(Next_Address), .clk(Clock), .clr(Clear));
  Adder adder_1 (.Src1(Next_Address), .Src2(18'h1), .Overflow(adder_1_overflow), .Result(adder_1_result));
  // also tied to GND on the sheet: adder_1_overflow
endmodule

module Extender (
  input  [9:0] in_1,
  output [17:0] out_2
);


  assign out_2 = {{9{in_1[9]}}, in_1[8:0]};
endmodule

// 10b Adder
module _10_Bit_Adder (
  input  [9:0] Src1,
  input  [9:0] Src2,
  output [9:0] Output,
  output Overflow
);

  wire full_adder_1_cout, full_adder_2_cout, full_adder_3_cout, full_adder_4_cout, full_adder_5_cout,
       full_adder_6_cout, full_adder_7_cout, full_adder_8_cout, full_adder_9_cout;

  Full_Adder full_adder_1 (.Cin(1'b0), .Src1(Src1[0]), .Src2(Src2[0]), .Sum(Output[0]), .Cout(full_adder_1_cout));
  Full_Adder full_adder_2 (
    .Cin(full_adder_1_cout), .Src1(Src1[1]), .Src2(Src2[1]), .Sum(Output[1]), .Cout(full_adder_2_cout));
  Full_Adder full_adder_3 (
    .Cin(full_adder_2_cout), .Src1(Src1[2]), .Src2(Src2[2]), .Sum(Output[2]), .Cout(full_adder_3_cout));
  Full_Adder full_adder_4 (
    .Cin(full_adder_3_cout), .Src1(Src1[3]), .Src2(Src2[3]), .Sum(Output[3]), .Cout(full_adder_4_cout));
  Full_Adder full_adder_5 (
    .Cin(full_adder_4_cout), .Src1(Src1[4]), .Src2(Src2[4]), .Sum(Output[4]), .Cout(full_adder_5_cout));
  Full_Adder full_adder_6 (
    .Cin(full_adder_5_cout), .Src1(Src1[5]), .Src2(Src2[5]), .Sum(Output[5]), .Cout(full_adder_6_cout));
  Full_Adder full_adder_7 (
    .Cin(full_adder_6_cout), .Src1(Src1[6]), .Src2(Src2[6]), .Sum(Output[6]), .Cout(full_adder_7_cout));
  Full_Adder full_adder_8 (
    .Cin(full_adder_7_cout), .Src1(Src1[7]), .Src2(Src2[7]), .Sum(Output[7]), .Cout(full_adder_8_cout));
  Full_Adder full_adder_9 (
    .Cin(full_adder_8_cout), .Src1(Src1[8]), .Src2(Src2[8]), .Sum(Output[8]), .Cout(full_adder_9_cout));
  Full_Adder full_adder_10 (.Cin(full_adder_9_cout), .Src1(Src1[9]), .Src2(Src2[9]), .Sum(Output[9]), .Cout(Overflow));
endmodule

module _1_bit_comparator (
  input  A,
  input  B,
  input  Equal,
  input  Greater,
  input  LessThan,
  output Equals,
  output Greater_2,
  output LessThan_2
);

  wire and_1_out, and_2_out, not_1_out, not_2_out, xnor_1_out;

  not not_1 (not_1_out, B);
  not not_2 (not_2_out, A);
  xnor xnor_1 (xnor_1_out, A, B);
  and and_1 (and_1_out, A, not_1_out, Equal);
  and and_2 (and_2_out, not_2_out, B, Equal);
  and and_3 (Equals, xnor_1_out, Equal);
  or or_1 (Greater_2, and_1_out, Greater);
  or or_2 (LessThan_2, and_2_out, LessThan);
endmodule

module _18_Bit_Comparator (
  input  [17:0] A,
  input  [17:0] B,
  output Equals,
  output Greater,
  output Less_Than
);

  wire n1_bit_comparator_1_equals, n1_bit_comparator_1_greater_2, n1_bit_comparator_1_lessthan_2,
       n1_bit_comparator_2_equals, n1_bit_comparator_2_greater_2, n1_bit_comparator_2_lessthan_2,
       n1_bit_comparator_3_equals, n1_bit_comparator_3_greater_2, n1_bit_comparator_3_lessthan_2,
       n1_bit_comparator_4_equals, n1_bit_comparator_4_greater_2, n1_bit_comparator_4_lessthan_2,
       n1_bit_comparator_5_equals, n1_bit_comparator_5_greater_2, n1_bit_comparator_5_lessthan_2,
       n1_bit_comparator_6_equals, n1_bit_comparator_6_greater_2, n1_bit_comparator_6_lessthan_2,
       n1_bit_comparator_7_equals, n1_bit_comparator_7_greater_2, n1_bit_comparator_7_lessthan_2,
       n1_bit_comparator_8_equals, n1_bit_comparator_8_greater_2, n1_bit_comparator_8_lessthan_2,
       n1_bit_comparator_9_equals, n1_bit_comparator_9_greater_2, n1_bit_comparator_9_lessthan_2,
       n1_bit_comparator_10_equals, n1_bit_comparator_10_greater_2, n1_bit_comparator_10_lessthan_2,
       n1_bit_comparator_11_equals, n1_bit_comparator_11_greater_2, n1_bit_comparator_11_lessthan_2,
       n1_bit_comparator_12_equals, n1_bit_comparator_12_greater_2, n1_bit_comparator_12_lessthan_2,
       n1_bit_comparator_13_equals, n1_bit_comparator_13_greater_2, n1_bit_comparator_13_lessthan_2,
       n1_bit_comparator_14_equals, n1_bit_comparator_14_greater_2, n1_bit_comparator_14_lessthan_2,
       n1_bit_comparator_15_equals, n1_bit_comparator_15_greater_2, n1_bit_comparator_15_lessthan_2,
       n1_bit_comparator_16_equals, n1_bit_comparator_16_greater_2, n1_bit_comparator_16_lessthan_2,
       n1_bit_comparator_17_equals, n1_bit_comparator_17_greater_2, n1_bit_comparator_17_lessthan_2,
       n1_bit_comparator_18_greater_2, n1_bit_comparator_18_lessthan_2;

  _1_bit_comparator u_1_bit_comparator_1 (
    .A(A[17]), .B(B[17]), .Equal(1'b1), .Greater(1'b0), .LessThan(1'b0), .Equals(n1_bit_comparator_1_equals),
    .Greater_2(n1_bit_comparator_1_greater_2), .LessThan_2(n1_bit_comparator_1_lessthan_2));
  _1_bit_comparator u_1_bit_comparator_2 (
    .A(A[16]), .B(B[16]), .Equal(n1_bit_comparator_1_equals), .Greater(n1_bit_comparator_1_greater_2),
    .LessThan(n1_bit_comparator_1_lessthan_2), .Equals(n1_bit_comparator_2_equals),
    .Greater_2(n1_bit_comparator_2_greater_2), .LessThan_2(n1_bit_comparator_2_lessthan_2));
  _1_bit_comparator u_1_bit_comparator_3 (
    .A(A[15]), .B(B[15]), .Equal(n1_bit_comparator_2_equals), .Greater(n1_bit_comparator_2_greater_2),
    .LessThan(n1_bit_comparator_2_lessthan_2), .Equals(n1_bit_comparator_3_equals),
    .Greater_2(n1_bit_comparator_3_greater_2), .LessThan_2(n1_bit_comparator_3_lessthan_2));
  _1_bit_comparator u_1_bit_comparator_4 (
    .A(A[14]), .B(B[14]), .Equal(n1_bit_comparator_3_equals), .Greater(n1_bit_comparator_3_greater_2),
    .LessThan(n1_bit_comparator_3_lessthan_2), .Equals(n1_bit_comparator_4_equals),
    .Greater_2(n1_bit_comparator_4_greater_2), .LessThan_2(n1_bit_comparator_4_lessthan_2));
  _1_bit_comparator u_1_bit_comparator_5 (
    .A(A[13]), .B(B[13]), .Equal(n1_bit_comparator_4_equals), .Greater(n1_bit_comparator_4_greater_2),
    .LessThan(n1_bit_comparator_4_lessthan_2), .Equals(n1_bit_comparator_5_equals),
    .Greater_2(n1_bit_comparator_5_greater_2), .LessThan_2(n1_bit_comparator_5_lessthan_2));
  _1_bit_comparator u_1_bit_comparator_6 (
    .A(A[12]), .B(B[12]), .Equal(n1_bit_comparator_5_equals), .Greater(n1_bit_comparator_5_greater_2),
    .LessThan(n1_bit_comparator_5_lessthan_2), .Equals(n1_bit_comparator_6_equals),
    .Greater_2(n1_bit_comparator_6_greater_2), .LessThan_2(n1_bit_comparator_6_lessthan_2));
  _1_bit_comparator u_1_bit_comparator_7 (
    .A(A[11]), .B(B[11]), .Equal(n1_bit_comparator_6_equals), .Greater(n1_bit_comparator_6_greater_2),
    .LessThan(n1_bit_comparator_6_lessthan_2), .Equals(n1_bit_comparator_7_equals),
    .Greater_2(n1_bit_comparator_7_greater_2), .LessThan_2(n1_bit_comparator_7_lessthan_2));
  _1_bit_comparator u_1_bit_comparator_8 (
    .A(A[10]), .B(B[10]), .Equal(n1_bit_comparator_7_equals), .Greater(n1_bit_comparator_7_greater_2),
    .LessThan(n1_bit_comparator_7_lessthan_2), .Equals(n1_bit_comparator_8_equals),
    .Greater_2(n1_bit_comparator_8_greater_2), .LessThan_2(n1_bit_comparator_8_lessthan_2));
  _1_bit_comparator u_1_bit_comparator_9 (
    .A(A[9]), .B(B[9]), .Equal(n1_bit_comparator_8_equals), .Greater(n1_bit_comparator_8_greater_2),
    .LessThan(n1_bit_comparator_8_lessthan_2), .Equals(n1_bit_comparator_9_equals),
    .Greater_2(n1_bit_comparator_9_greater_2), .LessThan_2(n1_bit_comparator_9_lessthan_2));
  _1_bit_comparator u_1_bit_comparator_10 (
    .A(A[8]), .B(B[8]), .Equal(n1_bit_comparator_9_equals), .Greater(n1_bit_comparator_9_greater_2),
    .LessThan(n1_bit_comparator_9_lessthan_2), .Equals(n1_bit_comparator_10_equals),
    .Greater_2(n1_bit_comparator_10_greater_2), .LessThan_2(n1_bit_comparator_10_lessthan_2));
  _1_bit_comparator u_1_bit_comparator_11 (
    .A(A[7]), .B(B[7]), .Equal(n1_bit_comparator_10_equals), .Greater(n1_bit_comparator_10_greater_2),
    .LessThan(n1_bit_comparator_10_lessthan_2), .Equals(n1_bit_comparator_11_equals),
    .Greater_2(n1_bit_comparator_11_greater_2), .LessThan_2(n1_bit_comparator_11_lessthan_2));
  Multiplexer #(.select(2), .enable("false")) multiplexer_1 (
    .in0(n1_bit_comparator_18_greater_2), .in1(1'b0), .in2(1'b1), .in3(n1_bit_comparator_18_greater_2),
    .out(Greater), .sel({B[17], A[17]}));
  Multiplexer #(.select(2), .enable("false")) multiplexer_2 (
    .in0(n1_bit_comparator_18_lessthan_2), .in1(1'b1), .in2(1'b0), .in3(n1_bit_comparator_18_lessthan_2),
    .out(Less_Than), .sel({B[17], A[17]}));
  _1_bit_comparator u_1_bit_comparator_12 (
    .A(A[6]), .B(B[6]), .Equal(n1_bit_comparator_11_equals), .Greater(n1_bit_comparator_11_greater_2),
    .LessThan(n1_bit_comparator_11_lessthan_2), .Equals(n1_bit_comparator_12_equals),
    .Greater_2(n1_bit_comparator_12_greater_2), .LessThan_2(n1_bit_comparator_12_lessthan_2));
  _1_bit_comparator u_1_bit_comparator_13 (
    .A(A[5]), .B(B[5]), .Equal(n1_bit_comparator_12_equals), .Greater(n1_bit_comparator_12_greater_2),
    .LessThan(n1_bit_comparator_12_lessthan_2), .Equals(n1_bit_comparator_13_equals),
    .Greater_2(n1_bit_comparator_13_greater_2), .LessThan_2(n1_bit_comparator_13_lessthan_2));
  _1_bit_comparator u_1_bit_comparator_14 (
    .A(A[4]), .B(B[4]), .Equal(n1_bit_comparator_13_equals), .Greater(n1_bit_comparator_13_greater_2),
    .LessThan(n1_bit_comparator_13_lessthan_2), .Equals(n1_bit_comparator_14_equals),
    .Greater_2(n1_bit_comparator_14_greater_2), .LessThan_2(n1_bit_comparator_14_lessthan_2));
  _1_bit_comparator u_1_bit_comparator_15 (
    .A(A[3]), .B(B[3]), .Equal(n1_bit_comparator_14_equals), .Greater(n1_bit_comparator_14_greater_2),
    .LessThan(n1_bit_comparator_14_lessthan_2), .Equals(n1_bit_comparator_15_equals),
    .Greater_2(n1_bit_comparator_15_greater_2), .LessThan_2(n1_bit_comparator_15_lessthan_2));
  _1_bit_comparator u_1_bit_comparator_16 (
    .A(A[2]), .B(B[2]), .Equal(n1_bit_comparator_15_equals), .Greater(n1_bit_comparator_15_greater_2),
    .LessThan(n1_bit_comparator_15_lessthan_2), .Equals(n1_bit_comparator_16_equals),
    .Greater_2(n1_bit_comparator_16_greater_2), .LessThan_2(n1_bit_comparator_16_lessthan_2));
  _1_bit_comparator u_1_bit_comparator_17 (
    .A(A[1]), .B(B[1]), .Equal(n1_bit_comparator_16_equals), .Greater(n1_bit_comparator_16_greater_2),
    .LessThan(n1_bit_comparator_16_lessthan_2), .Equals(n1_bit_comparator_17_equals),
    .Greater_2(n1_bit_comparator_17_greater_2), .LessThan_2(n1_bit_comparator_17_lessthan_2));
  _1_bit_comparator u_1_bit_comparator_18 (
    .A(A[0]), .B(B[0]), .Equal(n1_bit_comparator_17_equals), .Greater(n1_bit_comparator_17_greater_2),
    .LessThan(n1_bit_comparator_17_lessthan_2), .Equals(Equals), .Greater_2(n1_bit_comparator_18_greater_2),
    .LessThan_2(n1_bit_comparator_18_lessthan_2));
endmodule

module Branch_Circuit (
  input  [2:0] nzp,
  input  [17:0] OP1,
  input  [17:0] OP2,
  output Output
);

  wire and_1_out, and_2_out, and_3_out, n18_bit_comparator_1_equals, n18_bit_comparator_1_greater,
       n18_bit_comparator_1_less_than;

  _18_Bit_Comparator u_18_bit_comparator_1 (
    .A(OP1), .B(OP2), .Equals(n18_bit_comparator_1_equals), .Greater(n18_bit_comparator_1_greater),
    .Less_Than(n18_bit_comparator_1_less_than));
  and and_1 (and_1_out, nzp[2], n18_bit_comparator_1_less_than);
  and and_2 (and_2_out, nzp[1], n18_bit_comparator_1_equals);
  and and_3 (and_3_out, nzp[0], n18_bit_comparator_1_greater);
  or or_1 (Output, and_1_out, and_2_out, and_3_out);
endmodule

module Control_Unit (
  input  [3:0] OPcode,
  input  Branch_Output,
  input  Clock,
  output Use_Immediate,
  output Pc_Increment,
  output Pc_Enable_Input,
  output Enable_Write,
  output Data_Enable_Store,
  output Data_Enable_Load
);

  wire and_3_out, and_4_out, and_8_out, and_9_out, and_10_out, and_11_out, and_12_out, and_13_out,
       and_14_out, and_15_out, and_16_out, and_17_out, and_18_out, and_19_out, n0, n1, n2, not_1_out,
       not_2_out, not_3_out, not_4_out, not_5_out, not_6_out, not_7_out, not_8_out, not_9_out, not_10_out,
       not_11_out, not_12_out, not_13_out, not_14_out, not_15_out, not_16_out, not_17_out, not_18_out,
       not_19_out, not_20_out, not_21_out, not_22_out, not_23_out, or_3_out, or_4_out, or_5_out, or_6_out,
       or_7_out, or_8_out, s2_prime_s1_prime_s0_prime;
  wire [2:0] State;

  not not_1 (not_1_out, State[0]);
  not not_2 (not_2_out, State[2]);
  not not_3 (not_3_out, State[1]);
  not not_4 (not_4_out, State[0]);
  not not_5 (not_5_out, State[2]);
  not not_6 (not_6_out, State[0]);
  not not_7 (not_7_out, State[1]);
  not not_8 (not_8_out, State[1]);
  not not_9 (not_9_out, State[0]);
  not not_10 (not_10_out, State[1]);
  and and_1 (Use_Immediate, not_1_out, State[1], not_2_out);
  or or_1 (Pc_Increment, State[0], State[1], State[2]);
  and and_2 (Pc_Enable_Input, State[0], State[1], not_11_out);
  not not_11 (not_11_out, State[2]);
  and and_3 (and_3_out, State[0], not_3_out);
  and and_4 (and_4_out, not_4_out, State[1], not_5_out);
  and and_5 (Data_Enable_Store, not_6_out, not_7_out, State[2]);
  and and_6 (Data_Enable_Load, State[0], not_8_out, State[2]);
  and and_7 (s2_prime_s1_prime_s0_prime, not_9_out, not_10_out, not_12_out);
  not not_12 (not_12_out, State[2]);
  and and_8 (and_8_out, OPcode[3], OPcode[2]);
  and and_9 (and_9_out, OPcode[3], OPcode[1], OPcode[0]);
  not not_13 (not_13_out, OPcode[3]);
  and and_10 (and_10_out, not_13_out, not_14_out);
  not not_14 (not_14_out, OPcode[2]);
  not not_15 (not_15_out, OPcode[2]);
  and and_11 (and_11_out, not_15_out, not_16_out);
  not not_16 (not_16_out, OPcode[1]);
  not not_17 (not_17_out, OPcode[1]);
  not not_18 (not_18_out, OPcode[0]);
  and and_12 (and_12_out, OPcode[3], OPcode[1], OPcode[0]);
  not not_19 (not_19_out, Branch_Output);
  and and_13 (and_13_out, OPcode[3], OPcode[2]);
  and and_14 (and_14_out, OPcode[3], OPcode[1], OPcode[0]);
  not not_20 (not_20_out, OPcode[2]);
  and and_15 (and_15_out, OPcode[3], not_20_out, OPcode[1], not_21_out);
  not not_21 (not_21_out, OPcode[0]);
  not not_22 (not_22_out, OPcode[2]);
  not not_23 (not_23_out, OPcode[1]);
  or or_2 (Enable_Write, and_3_out, and_4_out);
  or or_3 (or_3_out, and_8_out, and_9_out);
  and and_16 (and_16_out, OPcode[3], not_17_out, not_18_out);
  or or_4 (or_4_out, and_13_out, and_14_out);
  or or_5 (or_5_out, and_15_out, and_17_out);
  and and_17 (and_17_out, OPcode[3], not_22_out, not_23_out, OPcode[0]);
  Register #(.width(3)) register_1 (.D({n2, n1, n0}), .en(1'b1), .Q(State), .clk(Clock));  // open: clr
  and and_18 (and_18_out, Branch_Output, or_3_out);
  or or_6 (or_6_out, OPcode[2], and_16_out, and_12_out);
  and and_19 (and_19_out, not_19_out, or_4_out);
  or or_7 (or_7_out, and_18_out, and_10_out, and_11_out);
  and and_20 (n1, or_6_out, s2_prime_s1_prime_s0_prime);
  or or_8 (or_8_out, and_19_out, or_5_out);
  and and_21 (n0, or_7_out, s2_prime_s1_prime_s0_prime);
  and and_22 (n2, or_8_out, s2_prime_s1_prime_s0_prime);

  // Other names for the same wires on the sheet: br = Branch_Output; Clk = Clock; New_State[2:0] = {n2, n1, n0};
  //   op0 = OPcode[0]; op1 = OPcode[1]; op2 = OPcode[2]; op3 = OPcode[3]
endmodule

module Is_Branch (
  input  [3:0] Opcode,
  output Is_Branch
);

  wire and_1_out, and_2_out, and_3_out, and_4_out, and_5_out, not_1_out, not_2_out, not_3_out, not_4_out,
       not_5_out;

  not not_1 (not_1_out, Opcode[2]);
  not not_2 (not_2_out, Opcode[0]);
  not not_3 (not_3_out, Opcode[1]);
  not not_4 (not_4_out, Opcode[1]);
  not not_5 (not_5_out, Opcode[0]);
  and and_1 (and_1_out, Opcode[0], Opcode[1], not_1_out, Opcode[3]);
  and and_2 (and_2_out, not_2_out, not_3_out, Opcode[2], Opcode[3]);
  and and_3 (and_3_out, Opcode[0], not_4_out, Opcode[2], Opcode[3]);
  and and_4 (and_4_out, not_5_out, Opcode[1], Opcode[2], Opcode[3]);
  and and_5 (and_5_out, Opcode[0], Opcode[1], Opcode[2], Opcode[3]);
  or or_1 (Is_Branch, and_1_out, and_2_out, and_3_out, and_4_out, and_5_out);
endmodule

// Ext
module _6_18_Extender (
  input  [5:0] Input,
  output [17:0] Output
);


  assign Output = {{13{Input[5]}}, Input[4:0]};
endmodule

module _14_18_Extender (
  input  [13:0] Input,
  output [17:0] Output
);


  assign Output = {{5{Input[13]}}, Input[12:0]};
endmodule

module _3_18_Extender (
  input  [2:0] Input,
  output [17:0] Output
);


  assign Output = {{16{Input[2]}}, Input[1:0]};
endmodule
